# Fritzing sketch RAZZO_circuito (saved by Fritzing 0.9.3b)
breadboards: 2

parts:
  Part1 = Arduino Nano (Rev3.0)
  Pro_Mini_3v3 = Arduino Pro Mini v13
  GY1 = MPU-6050 Board GY-521 [form="♀ (female)" package=THT]
  GY2 = MPU-6050 Board GY-521 [form="♀ (female)" package=THT]
  MASTER_(1) = STM32 Nucleo boards
  SLAVE_(2) = STM32 Nucleo boards
  LOGIC_LEVEL = Logic Level Converter
  Part3 = Bluetooth HC-05 Macho
  U1 = LIPO-110mAh [package=lipo-110]
  J1 = Basic Servo
  M1 = DC Motor
  L298N_mini = L298N DC motor driver
  pullup_resistors = Resistor [tolerance=±5% resistance=1k package="2512 [SMD]"]
  R2 = Resistor [tolerance=±5% resistance=1k package="2512 [SMD]"]
  Mission_Timer_led = LEDs [package=led10mm]
  R3 = Resistor [tolerance=±5% resistance=1k package="0603 [SMD]"]
  R4 = Resistor [tolerance=±5% resistance=220 package="0603 [SMD]"]
  common_clk_led = LEDs [package=led10mm]
  V_reg_5_0V1 = AMS1117 step down module
  V_reg_5_0V2 = AMS1117 step down module

nets:
  N1: Part1.D1/TX, Part3.RXD
  N2: Part1.D0/RX, Part3.TXD
  GND: Part1.GND, GY1.pin2, GY2.pin2, LOGIC_LEVEL.GND, Part3.GND, U1.-, J1.gnd, L298N_mini.GND, Mission_Timer_led.C, common_clk_led.C, V_reg_5_0V1.GND-, V_reg_5_0V2.GND-
  5V: Part1.5V, Pro_Mini_3v3.RAW, MASTER_(1).5V, SLAVE_(2).5V, LOGIC_LEVEL.HV, Part3.VCC, V_reg_5_0V2.VOUT+
  N3: Part1.A5, LOGIC_LEVEL.TX_HV
  N4: Part1.A4, LOGIC_LEVEL.RX_HV
  N5: Pro_Mini_3v3.VCC, LOGIC_LEVEL.LV, pullup_resistors.Pin_0, R2.Pin_0
  N6: Pro_Mini_3v3.A3, SLAVE_(2).PA5
  N7: Pro_Mini_3v3.A2, SLAVE_(2).PA4
  N8: Pro_Mini_3v3.A1, MASTER_(1).PA5
  N9: Pro_Mini_3v3.A0, MASTER_(1).PA4
  N10: Pro_Mini_3v3.D9_PWM, J1.pulse
  N11: Pro_Mini_3v3.D8, SLAVE_(2).PB12
  N12: Pro_Mini_3v3.D7, SLAVE_(2).PA12
  N13: Pro_Mini_3v3.D6_PWM, L298N_mini.IN1
  N14: Pro_Mini_3v3.D5_PWM, SLAVE_(2).PA11
  N15: Pro_Mini_3v3.D4, MASTER_(1).PA12
  N16: Pro_Mini_3v3.D3_PWM, MASTER_(1).PB12
  N17: Pro_Mini_3v3.D2, MASTER_(1).PA11
  N18: GY1.pin1, MASTER_(1).3V3
  N19: GY1.pin3, MASTER_(1).PB10
  N20: GY1.pin4, MASTER_(1).PB8
  N21: GY2.pin1, SLAVE_(2).3V3
  N22: GY2.pin3, SLAVE_(2).PB10
  N23: GY2.pin4, SLAVE_(2).PB8
  N24: MASTER_(1).CN_01, MASTER_(1).CN_02
  N25: MASTER_(1).CN_03, MASTER_(1).CN_04
  N26: MASTER_(1).JP5_2, MASTER_(1).JP5_03
  N27: MASTER_(1).GND#880, MASTER_(1).GND#881
  N28: MASTER_(1).GND#1149, MASTER_(1).GND#1150
  N29: MASTER_(1).PC9, SLAVE_(2).PC9, LOGIC_LEVEL.TX_LV, pullup_resistors.Pin_1
  N30: MASTER_(1).PA6, R4.Pin_1, common_clk_led.A
  N31: MASTER_(1).PA10, R3.Pin_0
  N32: MASTER_(1).PC12, SLAVE_(2).PC12, LOGIC_LEVEL.RX_LV, R2.Pin_1
  N33: SLAVE_(2).CN_01, SLAVE_(2).CN_02
  N34: SLAVE_(2).CN_03, SLAVE_(2).CN_04
  N35: SLAVE_(2).JP5_2, SLAVE_(2).JP5_03
  N36: SLAVE_(2).GND#880, SLAVE_(2).GND#881
  N37: SLAVE_(2).GND#1149, SLAVE_(2).GND#1150
  N38: SLAVE_(2).PC2, R4.Pin_0
  N39: U1.+, L298N_mini.12V, V_reg_5_0V1.VIN+, V_reg_5_0V2.VIN+
  N40: J1.vcc, V_reg_5_0V1.VOUT+
  N41: M1.pin_1, L298N_mini.OUT4
  N42: M1.pin_2, L298N_mini.OUT3
  N43: Mission_Timer_led.A, R3.Pin_1

notes:
  2S LIPO 350mAh
  IMU are overlapped

custom parts:
  MPU-6050 Board GY-521: Acelerometro y Giroscopio MPU-6050 Board GY-521
  L298N DC motor driver: 2x DC motor driver with 78M05 positive voltage regulator (7..35 V) L298N: max 46 V, 2 A Set 5 V Enable jumper to enable 5 V regultor (needed for the L298N) and +5 V output at screw terminal or supply external +5 V at screw terminal Set ENA and/or ENB to +5 V to enable motor permanently or supply ENA and/or ENB with PWM signal IN1 and IN2 set rotation directory for motor A (OUT1/OUT2) IN2 and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
